# Fritzing sketch schematics_mushroom (saved by Fritzing 0.9.3b)

parts:
  Part1 = Adafruit HUZZAH ESP8266 [part_number="Adafruit #2471"]
  neopixel1 = Neopixel Ring 16

nets:
  N1: Part1.VBAT, neopixel1.VCC
  GND: Part1.GND, neopixel1.GND
  N2: Part1.GPIO4, neopixel1.IN

custom parts:
  Adafruit HUZZAH ESP8266: Add Internet to your next project with an adorable, bite-sized WiFi microcontroller, at a price you like! The ESP8266 processor from Espressif is an 80 MHz microcontroller with a full WiFi front-end (both as client and access point) and TCP/IP stack with DNS support as well. While this chip has been very popular, its also been very difficult to use. Most of the low cost modules are not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
  Neopixel Ring 16: Neopixel Ring x16
